# Fritzing sketch weatherstation_mini (saved by Fritzing 0.9.3b)
perfboards: 1

parts:
  Bauteil3 = Arduino Pro Mini (3.3V)
  TRM1 = Terminal 2pin
  TRM2 = Terminal 2pin
  TRM3 = Terminal 2pin
  TRM5 = Terminal 2pin
  TRM6 = Terminal 2pin
  TRM7 = Terminal 2pin
  R24 = Resistor [tolerance=±5% resistance=47k package=THT]  # not connected
  R25 = Resistor [tolerance=±5% resistance=220 package=THT]
  R26 = Resistor [tolerance=±5% resistance=100k package=THT]
  C4 = Electrolytic Capacitor [capacitance=1µF package="100 mil [THT, electrolytic]"]
  R27 = Temperature Sensor (Thermistor) [thermistor_type=NTC package=THT]
  C5 = Ceramic Capacitor [capacitance="100 nF" package="1206 [SMD, multilayer]"]  # not connected
  R28 = Resistor [tolerance=±5% resistance=47k package=THT]  # not connected
  S3 = SWITCH-MOMENTARY-2 [package=reed_switch_plastic]
  D5 = Diode [package=diode-1n4148]
  R29 = Resistor [tolerance=±5% resistance=1k package=THT]
  D6 = Diode [package=diode-1n4148]  # not connected
  Q4 = NPN-Transistor [package="SOT-23 [SMD]"]
  R30 = Resistor [tolerance=±5% resistance=100k package=THT]  # not connected
  R31 = Resistor [tolerance=±5% resistance=47k package=THT]
  R32 = Resistor [tolerance=±5% resistance=1M package=THT]
  R33 = Resistor [tolerance=±5% resistance=1M package=THT]  # not connected
  STEPDOWN1 = Step Down 5V to 3.3V [package="DIP (Dual Inline) [THT]"]
  R34 = Resistor [tolerance=±5% resistance=220 package=THT]
  U1 = ESP8266 WiFi Module [part_number=ESP8266]
  JP1 = Header 1 [package=1x01_offset]
  JP2 = Header 1 [package=1x01_offset]
  JP3 = Header 1 [package=1x01_offset]
  M3 = BMP280
  Bauteil4 = BH1750
  JP5 = Header 1 [package=1x01_offset]
  JP6 = Header 1 [package=1x01_offset]
  JP7 = Header 1 [package=1x01_offset]
  JP8 = Header 1 [package=1x01_offset]
  JP9 = Header 1 [package=1x01_offset]
  JP10 = Header 1 [package=1x01_offset]
  JP12 = Header 1 [package=1x01_offset]  # not connected
  JP13 = Header 1 [package=1x01_offset]
  JP14 = Header 1 [package=1x01_offset]
  JP15 = Header 1 [package=1x01_offset]
  R35 = Resistor [tolerance=±5% resistance=47k package=THT]
  JP16 = Header 1 [package=1x01_offset]
  R36 = Resistor [tolerance=±5% resistance=47k package=THT]  # not connected
  JP17 = Header 1 [package=1x01_offset]  # not connected
  JP18 = Header 1 [package=1x01_offset]  # not connected
  JP19 = Header 1 [package=1x01_offset]  # not connected
  JP20 = Header 1 [package=1x01_offset]  # not connected

nets:
  N1: Bauteil3.TXO, JP5.1, JP10.1
  VCC: Bauteil3.VCC, TRM6.pin_2, STEPDOWN1.OUT, U1.CH_PD, JP2.1, M3.VIN, Bauteil4.VCC, JP9.1
  GND: Bauteil3.GND, TRM2.pin_1, C4.-, R27.pin_1, S3.1, R34.Pin_0, U1.GND, JP1.1, JP6.1, JP7.1, JP8.1, JP14.1
  N2: Bauteil3.A4, TRM7.pin_2, M3.SDA, Bauteil4.SDA
  N3: Bauteil3.A5, TRM7.pin_1, M3.SCL, Bauteil4.SCL
  N4: Bauteil3.A2, R32.Pin_1
  N5: Bauteil3.A1, TRM3.pin_2, R27.pin_0
  N6: Bauteil3.MOSI, R26.Pin_0
  N7: Bauteil3.D10, R25.Pin_1
  N8: Bauteil3.D7, U1.TXD
  N9: Bauteil3.D5, JP16.1
  N10: Bauteil3.D4, JP13.1
  N11: Bauteil3.D2, TRM5.pin_1
  N12: TRM1.pin_1, TRM2.pin_2, S3.2
  N13: TRM1.pin_2, Q4.2, R34.Pin_1
  N14: TRM3.pin_1, C4.+
  GND_2: TRM5.pin_2, TRM6.pin_1, M3.GND, Bauteil4.GND
  N15: D5.A, R29.Pin_1
  N16: Q4.1, STEPDOWN1.GND, JP3.1
  N17: R31.Pin_1, R35.Pin_1
  N18: R32.Pin_0, JP15.1

notes:
  Data - GND - 3V
  Pressure
  Light
  Rain Heater
  Rain
  Solarpower
  Rain (Reed)
  GND - Status - VCC
  DTR - RX - TX - CTS - 5V - GND
  Battery
  W132

custom parts:
  Terminal 2pin: 2-pin Terminal Block
  Step Down 5V to 3.3V: Step Down 5V to 3.3V 1A
  ESP8266 WiFi Module: Generic WiFi Module based on the ESP8266 with onboard PCB antenna and UART communications
  BMP280: Temperature Humidity Barometric presure Sensor, I2C
  BH1750: Light Sensor
