# Fritzing sketch weatherstation_mini2 (saved by Fritzing 0.9.3b)
perfboards: 1

parts:
  Bauteil3 = Arduino Pro Mini (3.3V)
  TRM1 = Terminal 2pin
  TRM2 = Terminal 2pin
  TRM3 = Terminal 2pin
  TRM5 = Terminal 2pin
  TRM6 = Terminal 2pin
  TRM7 = Terminal 2pin
  R25 = Resistor [tolerance=±5% resistance=220 package=THT]
  R26 = Resistor [tolerance=±5% resistance=100k package=THT]
  C4 = Electrolytic Capacitor [capacitance=1µF package="100 mil [THT, electrolytic]"]
  R27 = Temperature Sensor (Thermistor) [thermistor_type=NTC package=THT]
  C5 = Ceramic Capacitor [capacitance="100 nF" package="1206 [SMD, multilayer]"]  # not connected
  R28 = Resistor [tolerance=±5% resistance=47k package=THT]  # not connected
  S3 = SWITCH-MOMENTARY-2 [package=reed_switch_plastic]
  D5 = Diode [package=diode-1n4148]  # not connected
  R29 = Resistor [tolerance=±5% resistance=1k package=THT]
  D6 = Diode [package=diode-1n4148]  # not connected
  Q4 = NPN-Transistor [package="SOT-23 [SMD]"]
  R31 = Resistor [tolerance=±5% resistance=47k package=THT]  # not connected
  STEPDOWN1 = Step Down 5V to 3.3V [package="DIP (Dual Inline) [THT]"]
  R34 = Resistor [tolerance=±5% resistance=220 package=THT]
  U1 = ESP8266 WiFi Module [part_number=ESP8266]
  JP1 = Header 1 [package=1x01_offset]
  JP2 = Header 1 [package=1x01_offset]
  JP3 = Header 1 [package=1x01_offset]
  M3 = BMP280
  Bauteil4 = BH1750
  JP5 = Header 1 [package=1x01_offset]
  JP6 = Header 1 [package=1x01_offset]  # not connected
  JP7 = Header 1 [package=1x01_offset]
  JP8 = Header 1 [package=1x01_offset]
  JP9 = Header 1 [package=1x01_offset]
  JP10 = Header 1 [package=1x01_offset]
  JP12 = Header 1 [package=1x01_offset]
  R36 = Resistor [tolerance=±5% resistance=47k package=THT]
  JP17 = Header 1 [package=1x01_offset]
  JP18 = Header 1 [package=1x01_offset]
  JP19 = Header 1 [package=1x01_offset]
  JP20 = Header 1 [package=1x01_offset]  # not connected
  R37 = Resistor [tolerance=±5% resistance=1M package=THT]
  R38 = Resistor [tolerance=±5% resistance=1M package=THT]
  R24 = Resistor [tolerance=±5% resistance=47k package=THT]  # not connected
  R39 = Resistor [tolerance=±5% resistance=47k package=THT]  # not connected
  R41 = Resistor [tolerance=±5% resistance=220 package=THT]
  Bauteil5 = Adafruit VEML6075 UV Sensor Breakout [part_number=3964]
  C6 = Electrolytic Capacitor [capacitance=22µF package="100 mil [THT, electrolytic]"]  # not connected
  C7 = Ceramic Capacitor [capacitance="100 nF" package="1206 [SMD, multilayer]"]
  C9 = Electrolytic Capacitor [capacitance=1μF package="0405 [SMD, electrolytic]"]  # not connected

nets:
  N1: Bauteil3.TXO, JP10.1, JP12.1
  N2: Bauteil3.VCC, JP1.1, JP9.1
  N3: Bauteil3.GND, JP2.1, JP5.1, JP7.1, JP8.1
  N4: Bauteil3.A4, TRM7.pin_2, M3.SDA, Bauteil4.SDA, Bauteil5.SDA
  N5: Bauteil3.A5, TRM6.pin_2, TRM7.pin_1, M3.SCL, Bauteil4.SCL, Bauteil5.SCL
  N6: Bauteil3.A3, TRM3.pin_2, R27.pin_0
  N7: Bauteil3.A1, R37.Pin_0
  N8: Bauteil3.A0, JP19.1
  N9: Bauteil3.MISO, R36.Pin_1
  N10: Bauteil3.MOSI, R26.Pin_0
  N11: Bauteil3.D10, R25.Pin_1
  N12: Bauteil3.D6, U1.TXD
  N13: Bauteil3.D5, U1.CH_PD
  N14: Bauteil3.D4, R41.Pin_0
  N15: Bauteil3.D3, TRM1.pin_1, TRM2.pin_2, S3.2
  N16: Bauteil3.D2, TRM5.pin_1
  N17: TRM1.pin_2, R29.Pin_0, Q4.2, R34.Pin_1
  N18: TRM2.pin_1, C4.-, R27.pin_1, S3.1, R34.Pin_0
  N19: TRM3.pin_1, C4.+
  VIN: TRM5.pin_2, M3.VIN, Bauteil4.VCC, Bauteil5.3.3V
  GND: TRM6.pin_1, M3.GND, Bauteil4.GND, Bauteil5.GND
  N20: Q4.1, JP3.1
  N21: STEPDOWN1.OUT, U1.VCC
  N22: U1.GND, C7.1
  N23: JP17.1, R38.Pin_1
  N24: JP18.1, R37.Pin_1

notes:
  Data - 3V - GND
  Pressure
  Light
  Rain Heater
  Rain
  Solarpower
  Rain (Reed)
  GND - VCC - Done - Charge
  CTS - TX - RX - DTR - 5V - GND
  Battery
  W132
  UV

custom parts:
  Terminal 2pin: 2-pin Terminal Block
  Step Down 5V to 3.3V: Step Down 5V to 3.3V 1A
  ESP8266 WiFi Module: Generic WiFi Module based on the ESP8266 with onboard PCB antenna and UART communications
  BMP280: Temperature Humidity Barometric presure Sensor, I2C
  BH1750: Light Sensor
  Adafruit VEML6075 UV Sensor Breakout: This little sensor is a great way to add UVA and UVB light sensing to any microcontroller project. The VEML6075 from Vishay has both true UVA and UVB band light sensors and an I2C-controlled ADC that will take readings and integrate them. The sensor also comes with calibration registers so you can easily convert the UVA/UVB readings into the UV Index. Compared to our other UV sensors, this one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
