# Fritzing sketch weatherstation_mini6 (saved by Fritzing 0.9.3b)
perfboards: 2

parts:
  TRM1 = Terminal 2pin
  TRM2 = Terminal 2pin
  TRM3 = Terminal 2pin
  TRM5 = Terminal 2pin
  TRM6 = Terminal 2pin
  TRM7 = Terminal 2pin
  R26 = Resistor [tolerance=±5% resistance=100k package=THT]
  C4 = Electrolytic Capacitor [capacitance=1µF package="100 mil [THT, electrolytic]"]
  R27 = Temperature Sensor (Thermistor) [thermistor_type=NTC package=THT]
  C5 = Ceramic Capacitor [capacitance="100 nF" package="1206 [SMD, multilayer]"]
  R28 = Resistor [tolerance=±5% resistance=47k package=THT]
  S3 = SWITCH-MOMENTARY-2 [package=reed_switch_plastic]
  D6 = Diode [package=diode-1n4148]
  R31 = Resistor [tolerance=±5% resistance=47k package=THT]
  R34 = Resistor [tolerance=±5% resistance=220 package=THT]
  M3 = BMP280
  Bauteil4 = BH1750
  JP20 = Header 1 [package=1x01_offset]  # not connected
  R24 = Resistor [tolerance=±5% resistance=47k package=THT]  # not connected
  Bauteil5 = Adafruit VEML6075 UV Sensor Breakout [part_number=3964]
  C10 = Ceramic Capacitor [capacitance="100 nF" package="1206 [SMD, multilayer]"]  # not connected
  R41 = Resistor [tolerance=±5% resistance=100k package=THT]
  Bauteil3 = Arduino Pro Mini (3.3V)
  JP19 = Header 1 [package=1x01_offset]  # not connected
  JP21 = Header 1 [package=1x01_offset]  # not connected
  JP22 = Header 1 [package=1x01_offset]  # not connected
  JP23 = Header 1 [package=1x01_offset]
  JP24 = Header 1 [package=1x01_offset]
  JP25 = Header 1 [package=1x01_offset]
  JP26 = Header 1 [package=1x01_offset]
  JP27 = Header 1 [package=1x01_offset]  # not connected
  JP28 = Header 1 [package=1x01_offset]  # not connected
  JP29 = Header 1 [package=1x01_offset]  # not connected
  JP30 = Header 1 [package=1x01_offset]  # not connected
  JP31 = Header 1 [package=1x01_offset]  # not connected
  JP32 = Header 1 [package=1x01_offset]  # not connected
  JP33 = Header 1 [package=1x01_offset]
  JP34 = Header 1 [package=1x01_offset]  # not connected
  JP35 = Header 1 [package=1x01_offset]
  TRM13 = Terminal 2pin
  JP36 = Header 1 [package=1x01_offset]  # not connected
  JP37 = Header 1 [package=1x01_offset]
  JP38 = Header 1 [package=1x01_offset]
  JP39 = Header 1 [package=1x01_offset]  # not connected
  JP40 = Header 1 [package=1x01_offset]
  R47 = Resistor [tolerance=±5% resistance=47k package=THT]
  JP41 = Header 1 [package=1x01_offset]
  JP42 = Header 1 [package=1x01_offset]
  JP43 = Header 1 [package=1x01_offset]  # not connected
  JP44 = Header 1 [package=1x01_offset]
  Q11 = Basic FET P-Channel [package="TO220 [THT]"]
  Q10 = NPN-Transistor [package="SOT-23 [SMD]"]

nets:
  N1: TRM1.pin_1, TRM2.pin_2, S3.2, R31.Pin_0
  N2: TRM1.pin_2, R34.Pin_1
  N3: TRM2.pin_1, C4.-, R27.pin_1, C5.0, S3.1, R34.Pin_0
  N4: TRM3.pin_1, C4.+, Bauteil3.A1
  N5: TRM3.pin_2, R27.pin_0, Bauteil3.A2
  N6: TRM5.pin_1, Bauteil3.D3
  N7: TRM5.pin_2, M3.VIN
  GND: TRM6.pin_1, M3.GND, Bauteil4.GND, Bauteil5.GND, Bauteil3.GND
  N8: TRM6.pin_2, TRM7.pin_1, M3.SCL, Bauteil4.SCL, Bauteil5.SCL
  N9: TRM7.pin_2, M3.SDA, Bauteil4.SDA, Bauteil4.ADDR, Bauteil5.SDA, Bauteil3.A4
  N10: R26.Pin_1, Bauteil3.D8
  N11: R28.Pin_0, Bauteil3.D9
  N12: D6.C, JP41.1
  VCC: Bauteil4.VCC, Bauteil5.3.3V
  N13: R41.Pin_0, Bauteil3.D7
  N14: R41.Pin_1, JP42.1
  N15: Bauteil3.VCC, JP38.1
  N16: Bauteil3.A0, JP23.1
  N17: Bauteil3.MISO, JP24.1
  N18: Bauteil3.MOSI, JP25.1
  N19: Bauteil3.D10, JP26.1
  N20: Bauteil3.D2, JP33.1
  N21: JP35.1, TRM13.pin_2
  N22: TRM13.pin_1, JP37.1
  N23: JP40.1, JP44.1
  N24: R47.Pin_1, Q11.gate, Q10.2

notes:
  Data - 3V - GND
  Pressure
  Light
  Rain Heater
  Rain
  Solarpower
  Rain (Reed)
  Rain Heater 30Ohm
  W132
  UV
  3V-8V

custom parts:
  Terminal 2pin: 2-pin Terminal Block
  BMP280: Temperature Humidity Barometric presure Sensor, I2C
  BH1750: Light Sensor
  Adafruit VEML6075 UV Sensor Breakout: This little sensor is a great way to add UVA and UVB light sensing to any microcontroller project. The VEML6075 from Vishay has both true UVA and UVB band light sensors and an I2C-controlled ADC that will take readings and integrate them. The sensor also comes with calibration registers so you can easily convert the UVA/UVB readings into the UV Index. Compared to our other UV sensors, this one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
